// Logisim project ece385_lab1(2).circ as structural Verilog: 1 circuit, main circuit main
// 2
module main (
);

  wire clock_1_out, dipswitch_1_p1, dipswitch_1_p2, dipswitch_1_p3, dipswitch_1_p4, dipswitch_2_sw1,
       dipswitch_3_p1, dipswitch_3_p2, dipswitch_3_p3, dipswitch_3_p4, dipswitch_5_p3, multiplexer_1_out,
       n7400_1_pin8, n7400_1_pin11, n7400_2_pin4, n7400_2_pin6, n7400_2_pin8, n7400_2_pin11, n7400_2_pin12,
       n7400_3_pin6, n7400_3_pin11, n7400_3_pin12, n7402_1_pin9, n7402_1_pin10, n7402_1_pin11, n7402_1_pin12,
       n7402_1_pin13, n7402_3_pin1, n7402_3_pin8, n7402_3_pin10, n7402_3_pin12, n7402_3_pin13, n7486_1_pin3,
       n7486_1_pin11, n74163_1_pin7, n74163_1_pin9, n74163_1_pin13, n74163_1_pin14, REG_A_p4, REG_B_p4,
       REG_B_p9, REG_B_p14, REG_B_p15, REG_B_p16, REG_B_p17;
  wire [1:0] dipswitch_5_p1, dipswitch_6_p1;

  _7402 #(.ShowInternalStructure("true")) u_7402_1 (
    .pin13(n7402_1_pin13), .pin12(n7402_1_pin12), .pin11(n7402_1_pin11), .pin10(n7402_1_pin10),
    .pin9(n7402_1_pin9), .pin8(n7402_1_pin11));  // open: pin1, pin2, pin3, pin4, pin5, pin6
  _7400 #(.ShowInternalStructure("true")) u_7400_1 (
    .pin13(n7402_1_pin13), .pin12(n7402_1_pin13), .pin11(n7400_1_pin11), .pin10(n7402_1_pin10),
    .pin9(n7402_1_pin10), .pin8(n7400_1_pin8));  // open: pin1, pin2, pin3, pin4, pin5, pin6
  // DipSwitch #(.number(4)) dipswitch_1: pin names not known; wires that end beside it: dipswitch_1_p1, dipswitch_1_p2, dipswitch_1_p3, dipswitch_1_p4
  DipSwitch #(.number(2)) dipswitch_2 (.sw1(dipswitch_2_sw1));  // open: sw2
  Clock clock_1 (.out(clock_1_out));
  // DipSwitch #(.number(4)) dipswitch_3: pin names not known; wires that end beside it: dipswitch_3_p1, dipswitch_3_p2, dipswitch_3_p3, dipswitch_3_p4
  Button button_1 (.out(n7402_1_pin12));
  // Shift_Register #(.length(4)) REG_A: pin names not known; wires that end beside it: n7402_1_pin12, n7400_1_pin11, clock_1_out, REG_A_p4, dipswitch_1_p1
  // Shift_Register #(.length(4)) REG_B: pin names not known; wires that end beside it: dipswitch_1_p2, dipswitch_1_p3, dipswitch_1_p4, REG_B_p4, REG_B_p4, n7402_1_pin9, n7400_1_pin8, clock_1_out, REG_B_p9, dipswitch_3_p1, dipswitch_3_p2, dipswitch_3_p3, dipswitch_3_p4, REG_B_p14, REG_B_p15, REG_B_p16, REG_B_p17
  Button button_2 (.out(n7402_1_pin9));
  _74163 #(.ShowInternalStructure("true")) u_74163_1 (
    .pin2(clock_1_out), .pin7(n74163_1_pin7), .pin14(n74163_1_pin14), .pin13(n74163_1_pin13),
    .pin10(n7402_1_pin11), .pin9(n74163_1_pin9));  // open: pin1, pin3, pin4, pin5, pin6, pin15, pin12, pin11
  LED led_1 (.in(REG_B_p17));
  LED led_2 ();  // open: in
  LED led_3 ();  // open: in
  LED led_4 ();  // open: in
  LED led_5 (.in(n7400_2_pin12));
  LedBar #(.matrixcols(2)) ledbar_1 (.led0(n74163_1_pin13), .led1(n74163_1_pin14));
  DipSwitch #(.number(4)) dipswitch_4 (.sw2(n74163_1_pin7), .sw4(n74163_1_pin9));  // open: sw1, sw3
  LED led_6 (.in(REG_B_p14));
  LED led_7 (.in(REG_B_p15));
  LED led_8 (.in(REG_B_p16));
  _7400 #(.ShowInternalStructure("true")) u_7400_2 (
    .pin4(n7400_2_pin4), .pin5(n7400_2_pin4), .pin6(n7400_2_pin6), .pin13(REG_B_p17), .pin12(n7400_2_pin12),
    .pin11(n7400_2_pin11), .pin10(n7400_2_pin11), .pin9(n7400_2_pin11), .pin8(n7400_2_pin8));  // open: pin1, pin2, pin3
  _7402 #(.ShowInternalStructure("true")) u_7402_2 (
    .pin13(n7400_2_pin4), .pin12(n7400_2_pin12), .pin11(REG_B_p17));  // open: pin1, pin2, pin3, pin4, pin5, pin6, pin10, pin9, pin8
  _7402 #(.ShowInternalStructure("true")) u_7402_3 (
    .pin1(n7402_3_pin1), .pin2(n74163_1_pin13), .pin3(n74163_1_pin14), .pin13(n7402_3_pin13),
    .pin12(n7402_3_pin12), .pin11(dipswitch_2_sw1), .pin10(n7402_3_pin10), .pin9(n7402_3_pin12),
    .pin8(n7402_3_pin8));  // open: pin4, pin5, pin6
  _7400 #(.ShowInternalStructure("true")) u_7400_3 (
    .pin1(n7402_3_pin1), .pin2(n7402_3_pin1), .pin3(n7402_3_pin12), .pin4(n7402_3_pin13),
    .pin5(n7402_3_pin13), .pin6(n7400_3_pin6), .pin13(dipswitch_2_sw1), .pin12(n7400_3_pin12),
    .pin11(n7400_3_pin11), .pin10(n7400_3_pin11), .pin9(n7400_3_pin11), .pin8(n7402_3_pin8));
  _7474 #(.ShowInternalStructure("true")) u_7474_1 (
    .pin2(n7400_3_pin6), .pin3(clock_1_out), .pin6(n7400_3_pin12));  // open: pin1, pin4, pin5, pin13, pin12, pin11, pin10, pin9, pin8
  LedBar #(.matrixcols(1)) ledbar_2 (.led0(n7400_3_pin6));
  // DipSwitch #(.number(3)) dipswitch_5: pin names not known; wires that end beside it: dipswitch_5_p1[0], dipswitch_5_p1[1], dipswitch_5_p3
  Multiplexer #(.select(2)) multiplexer_1 (
    .in0(n7400_2_pin8), .in1(n7400_2_pin6), .in2(n7486_1_pin3), .in3(1'b1), .out(multiplexer_1_out),
    .sel(dipswitch_5_p1));
  _7486 #(.ShowInternalStructure("true")) u_7486_1 (
    .pin1(n7400_2_pin12), .pin2(REG_B_p17), .pin3(n7486_1_pin3), .pin13(multiplexer_1_out),
    .pin12(dipswitch_5_p3), .pin11(n7486_1_pin11));  // open: pin4, pin5, pin6, pin10, pin9, pin8
  _7400 #(.ShowInternalStructure("true")) u_7400_4 (
    .pin13(n7402_3_pin10), .pin12(n7402_3_pin10), .pin11(n7402_1_pin11));  // open: pin1, pin2, pin3, pin4, pin5, pin6, pin10, pin9, pin8
  // DipSwitch #(.number(2)) dipswitch_6: pin names not known; wires that end beside it: dipswitch_6_p1[0], dipswitch_6_p1[1]
  Multiplexer #(.select(2)) multiplexer_2 (
    .in0(REG_B_p17), .in1(REG_B_p17), .in2(n7486_1_pin11), .in3(n7400_2_pin12), .out(REG_A_p4),
    .sel(dipswitch_6_p1));
  Multiplexer #(.select(2)) multiplexer_3 (
    .in0(n7400_2_pin12), .in1(n7486_1_pin11), .in2(n7400_2_pin12), .in3(REG_B_p17), .out(REG_B_p9),
    .sel(dipswitch_6_p1));

  // Notes on the sheet:
  //   S
  //   Execute
  //   A'
  //   B'
  //   C1
  //   B
  //   C0
  //   A
  //   F0
  //   Q+
  //   F1
  //   F2
  //   f(A,B)
  //   R0
  //   S
  //   R1
  //   A'
  //   B'
endmodule
