// Logisim project lab1_diagram.circ as structural Verilog: 1 circuit, main circuit main
module main (
  input  in_1,
  input  in_2,
  input  in_3,
  input  in_4
);

  wire button_1_out, clock_1_out, dipswitch_1_sw1, dipswitch_2_p1, dipswitch_2_p2, dipswitch_2_p3,
       dipswitch_2_p4, dipswitch_3_p2, dipswitch_3_p3, dipswitch_3_p4, dipswitch_3_p5, n7400_1_pin4,
       n7400_1_pin6, n7400_1_pin11, n7400_1_pin13, n7400_2_pin2, n7400_2_pin3, n7400_2_pin6, n7400_2_pin10,
       n7400_2_pin11, n7400_2_pin13, n7400_3_pin3, n7400_3_pin6, n7400_3_pin11, n7400_3_pin13, n7402_1_pin2,
       n7402_1_pin3, n7474_1_pin1, n7474_1_pin4, n7486_1_pin8, n7486_1_pin9, n7486_1_pin10, n7486_1_pin11,
       n74161_1_pin7, n74161_1_pin9, n74161_1_pin10, n74161_1_pin11, n74161_1_pin12, n74161_1_pin13,
       n74161_1_pin14, shift_register_1_p1, shift_register_1_p6, shift_register_1_p11, shift_register_1_p12,
       shift_register_1_p13, shift_register_1_p14, shift_register_2_p1, shift_register_2_p6,
       shift_register_2_p11, shift_register_2_p12, shift_register_2_p13, shift_register_2_p14, undriven;
  wire [1:0] dipswitch_4_sw3, dipswitch_5_sw2;

  LedBar #(.matrixcols(1)) ledbar_1 (.led0(n7400_2_pin11));
  Button button_1 (.out(button_1_out));
  DipSwitch #(.number(2)) dipswitch_1 (.sw1(dipswitch_1_sw1));  // open: sw2
  // DipSwitch #(.number(4)) dipswitch_2: pin names not known; wires that end beside it: dipswitch_2_p1, dipswitch_2_p2, dipswitch_2_p3, dipswitch_2_p4, 1'b1
  _7400 #(.ShowInternalStructure("true")) u_7400_1 (
    .pin4(n7400_1_pin4), .pin5(n7400_1_pin4), .pin6(n7400_1_pin6), .pin13(n7400_1_pin13),
    .pin12(n7400_1_pin13), .pin11(n7400_1_pin11));  // open: pin1, pin2, pin3, pin10, pin9, pin8
  _7402 #(.ShowInternalStructure("true")) u_7402_1 (
    .pin1(n7400_1_pin4), .pin2(n7402_1_pin2), .pin3(n7402_1_pin3), .pin13(n7400_1_pin13),
    .pin12(button_1_out), .pin11(n7402_1_pin3));  // open: pin4, pin5, pin6, pin10, pin9, pin8
  Button button_2 (.out(n7402_1_pin2));
  Clock clock_1 (.out(clock_1_out));
  // DipSwitch #(.number(4)) dipswitch_3: pin names not known; wires that end beside it: 1'b1, dipswitch_3_p2, dipswitch_3_p3, dipswitch_3_p4, dipswitch_3_p5
  // Shift_Register #(.length(4)) shift_register_1: pin names not known; wires that end beside it: shift_register_1_p1, shift_register_1_p1, n7402_1_pin2, n7400_1_pin6, clock_1_out, shift_register_1_p6, dipswitch_2_p1, dipswitch_2_p2, dipswitch_2_p3, dipswitch_2_p4, shift_register_1_p11, shift_register_1_p12, shift_register_1_p13, shift_register_1_p14
  // Shift_Register #(.length(4)) shift_register_2: pin names not known; wires that end beside it: shift_register_2_p1, shift_register_2_p1, button_1_out, n7400_1_pin11, clock_1_out, shift_register_2_p6, dipswitch_3_p2, dipswitch_3_p3, dipswitch_3_p4, dipswitch_3_p5, shift_register_2_p11, shift_register_2_p12, shift_register_2_p13, shift_register_2_p14
  LedBar ledbar_2 (
    .led0(shift_register_2_p14), .led1(shift_register_2_p13), .led2(shift_register_2_p12),
    .led3(shift_register_2_p11), .led4(shift_register_1_p14), .led5(shift_register_1_p13),
    .led6(shift_register_1_p12), .led7(shift_register_1_p11));
  _74161 #(.ShowInternalStructure("true")) u_74161_1 (
    .pin1(n7402_1_pin3), .pin2(clock_1_out), .pin3(in_1), .pin4(in_2), .pin5(in_3), .pin6(in_4),
    .pin7(n74161_1_pin7), .pin14(n74161_1_pin14), .pin13(n74161_1_pin13), .pin12(n74161_1_pin12),
    .pin11(n74161_1_pin11), .pin10(n74161_1_pin10), .pin9(n74161_1_pin9));  // open: pin15
  _7400 #(.ShowInternalStructure("true")) u_7400_2 (
    .pin1(dipswitch_1_sw1), .pin2(n7400_2_pin2), .pin3(n7400_2_pin3), .pin4(n7400_2_pin3),
    .pin5(n7400_2_pin3), .pin6(n7400_2_pin6), .pin13(n7400_2_pin13), .pin12(n7400_2_pin13),
    .pin11(n7400_2_pin11), .pin10(n7400_2_pin10), .pin9(n7400_2_pin10), .pin8(n7402_1_pin3));
  _7400 #(.ShowInternalStructure("true")) u_7400_3 (
    .pin1(shift_register_1_p14), .pin2(shift_register_2_p14), .pin3(n7400_3_pin3), .pin4(n7400_3_pin3),
    .pin5(n7400_3_pin3), .pin6(n7400_3_pin6), .pin13(n7400_3_pin13), .pin12(n7400_3_pin13),
    .pin11(n7400_3_pin11));  // open: pin10, pin9, pin8
  // _7402 #(.ShowInternalStructure("true")) 7402_2: pin names not known; wires that end beside it: 1'b1, n7400_3_pin13, shift_register_1_p14, shift_register_2_p14, 1'b0
  _7486 #(.ShowInternalStructure("true")) u_7486_1 (
    .pin13(shift_register_2_p14), .pin12(shift_register_1_p14), .pin11(n7486_1_pin11), .pin10(n7486_1_pin10),
    .pin9(n7486_1_pin9), .pin8(n7486_1_pin8));  // open: pin1, pin2, pin3, pin4, pin5, pin6
  _7427 #(.ShowInternalStructure("true")) u_7427_1 (
    .pin1(n74161_1_pin14), .pin2(n74161_1_pin13), .pin3(n74161_1_pin14), .pin4(n74161_1_pin13),
    .pin5(n7400_2_pin6), .pin6(n7400_2_pin10), .pin13(dipswitch_1_sw1), .pin12(n7400_2_pin13));  // open: pin11, pin10, pin9, pin8
  Multiplexer #(.select(2)) multiplexer_1 (
    .in0(n7400_3_pin6), .in1(n7400_3_pin11), .in2(n7486_1_pin11), .in3(undriven), .out(n7486_1_pin9),
    .sel(dipswitch_4_sw3));
  DipSwitch #(.number(3)) dipswitch_4 (.sw1(n7486_1_pin10), .sw2(dipswitch_4_sw3[1]), .sw3(dipswitch_4_sw3[0]));
  _7474 #(.ShowInternalStructure("true")) u_7474_1 (
    .pin1(n7474_1_pin1), .pin2(n7400_2_pin11), .pin3(clock_1_out), .pin4(n7474_1_pin4), .pin6(n7400_2_pin2));  // open: pin5, pin13, pin12, pin11, pin10, pin9, pin8
  Multiplexer #(.select(2)) multiplexer_2 (
    .in0(shift_register_1_p14), .in1(shift_register_1_p14), .in2(n7486_1_pin8), .in3(shift_register_2_p14),
    .out(shift_register_1_p6), .sel(dipswitch_5_sw2));
  Multiplexer #(.select(2)) multiplexer_3 (
    .in0(shift_register_2_p14), .in1(n7486_1_pin8), .in2(shift_register_2_p14), .in3(shift_register_1_p14),
    .out(shift_register_2_p6), .sel(dipswitch_5_sw2));
  DipSwitch #(.number(2)) dipswitch_5 (.sw1(dipswitch_5_sw2[1]), .sw2(dipswitch_5_sw2[0]));
  // also tied to VCC on the sheet: {n74161_1_pin7, n74161_1_pin10, n74161_1_pin9, n7474_1_pin1, n7474_1_pin4}

  // Notes on the sheet:
  //   load B
  //   Q
  //   E
  //   load A
  //   clock
  //   S
  //   D3
  //   D2
  //   D1
  //   D0
  //   RegA
  //   RegB
  //   A
  //   B
  //   F2
  //   F1
  //   F0
  //   R0
  //   R1
endmodule
